# Fritzing sketch arduino_keypad_lcd (saved by Fritzing 0.9.3b)

parts:
  LCD1 = LCD screen
  Part1 = Arduino Uno (Rev3)
  U1 = POT [package=pot_mammoth]
  Keypad4x1 = Keypad Membran 4x4

nets:
  N1: LCD1.V0, U1.A
  N2: LCD1.RS, Part1.D8
  N3: LCD1.R/W, U1.E
  N4: LCD1.E, Part1.D9_PWM
  N5: LCD1.DB4, Part1.D10_PWM/SS
  N6: LCD1.DB5, Part1.D11_PWM/MOSI
  N7: LCD1.DB6, Part1.D12/MISO
  N8: LCD1.DB7, Part1.D13/SCK
  N9: LCD1.LED+, Part1.5V
  N10: LCD1.LED-, Part1.GND
  N11: Part1.D0/RX, Keypad4x1.Pin1
  N12: Part1.D1/TX, Keypad4x1.Pin2
  N13: Part1.D2, Keypad4x1.Pin3
  N14: Part1.D3_PWM, Keypad4x1.Pin4
  N15: Part1.D4, Keypad4x1.Pin5
  N16: Part1.D5_PWM, Keypad4x1.Pin6
  N17: Part1.D6_PWM, Keypad4x1.Pin7
  N18: Part1.D7, Keypad4x1.Pin8

custom parts:
  Keypad Membran 4x4: Membrane Keypad 4x4 Matrix
